# Fritzing sketch Schma_AGV (saved by Fritzing 0.9.3b)
breadboards: 1

parts:
  Parte1 = Arduino Uno (Rev3) - ICSP
  M4 = DC Motor
  L298N1 = L298N DC motor driver
  M2 = DC Motor
  M5 = DC Motor
  M6 = DC Motor
  U1 = LIPO-2000mAh [package=lipo-2000]
  Parte2 = Bluetooth HC-05 Macho
  hc-sr1 = hc-sr04
  hc-sr2 = hc-sr04
  M7 = fc-51 [package=THT]
  M8 = fc-51 [package=THT]
  M9 = fc-51 [package=THT]

nets:
  N1: Parte1.A0, M9.pin1
  N2: Parte1.A1, M8.pin1
  N3: Parte1.A2, M7.pin1
  N4: Parte1.ICSP_MISO, Parte1.D12/MISO, hc-sr2.Echo
  N5: Parte1.D8, L298N1.IN3
  N6: Parte1.D9_PWM, L298N1.IN4
  N7: Parte1.D10_PWM/SS, L298N1.ENB
  N8: Parte1.D13/SCK, hc-sr2.Trig
  N9: Parte1.D0/RX, Parte2.TXD
  N10: Parte1.D1/TX, Parte2.RXD
  N11: Parte1.D2, hc-sr1.Echo
  N12: Parte1.D3_PWM, hc-sr1.Trig
  N13: Parte1.D5_PWM, L298N1.ENA
  N14: Parte1.D6_PWM, L298N1.IN1
  N15: Parte1.D7, L298N1.IN2
  3V3: Parte1.3V3, L298N1.12V, U1.+
  GND: Parte1.GND, L298N1.GND, U1.-
  VIN: Parte1.VIN, L298N1.5V
  N16: M4.pin_1, L298N1.OUT3, M6.pin_1
  N17: M4.pin_2, L298N1.OUT4, M6.pin_2
  N18: L298N1.OUT1, M2.pin_2, M5.pin_2
  N19: L298N1.OUT2, M2.pin_1, M5.pin_1
  VCC: Parte2.VCC, hc-sr1.VCC, hc-sr2.VCC, M7.pin3, M8.pin3, M9.pin3
  GND_2: Parte2.GND, hc-sr1.GND, hc-sr2.GND, M7.pin2, M8.pin2, M9.pin2

custom parts:
  L298N DC motor driver: 2x DC motor driver with 78M05 positive voltage regulator (7..35 V) L298N: max 46 V, 2 A Set 5 V Enable jumper to enable 5 V regultor (needed for the L298N) and +5 V output at screw terminal or supply external +5 V at screw terminal Set ENA and/or ENB to +5 V to enable motor permanently or supply ENA and/or ENB with PWM signal IN1 and IN2 set rotation directory for motor A (OUT1/OUT2) IN2 and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
